# Fritzing sketch PillChecker (saved by Fritzing 0.9.4)
breadboards: 1

parts:
  부품1 = Arduino Uno (Rev3)
  J1 = Piezo Speaker
  R1 = Resistor [tolerance=±10% resistance=220 package=THT]
  J2 = Infrared Proximity Sensor
  S1 = Pushbutton [package="[THT]"]
  R2 = Resistor [tolerance=±5% resistance=1k package=THT]
  J3 = Basic Servo  # not connected
  LED1 = RGB LED (com. cathode, rgb) [package="5 mm [THT]"]
  R3 = Photocell (LDR) [package=THT]
  S2 = Pushbutton [package="[THT]"]
  R4 = Resistor [tolerance=±5% resistance=1k package=THT]
  R5 = Resistor [tolerance=±5% resistance=220 package=THT]

nets:
  N1: 부품1.A1, R3.pin_1, R5.Pin_1
  GND: 부품1.GND, J1.pin1, J2.GND, S1.Pin_3, S1.Pin_4, S2.Pin_1, S2.Pin_2, R5.Pin_0
  N2: 부품1.D3_PWM, J1.pin2
  N3: 부품1.D4, S1.Pin_1, S1.Pin_2, R2.Pin_0
  N4: 부품1.D5_PWM, LED1.red_anode
  N5: 부품1.D6_PWM, LED1.green_anode
  5V: 부품1.RESET, 부품1.5V, R1.Pin_1, J2.Vcc, R2.Pin_1, R3.pin_0, S2.Pin_3, S2.Pin_4, R4.Pin_0, R4.Pin_1
  N6: R1.Pin_0, LED1.common_cathode

// code stored in the sketch: PillChecker.ino
int pill_sensor = A0;
int warn_LED = 5;
int warn_piezo = 3;
int pill_ejectSwitch = 4;

int tones[] = { 261, 294, 330, 349, 392, 440, 494, 523};

void setup() {
	pinMode(pill_sensor, INPUT);
	pinMode(pill_ejectSwitch, INPUT);
	pinMode(warn_LED, OUTPUT);
	pinMode(warn_piezo, OUTPUT);
}

void loop() {
	if (/*TODO: IR SENSOR ACT CODE */ pill_ejectSwitch == LOW) {
		int i = 0;
		digitalWrite(warn_LED, HIGH);
		tone(warn_piezo, tones[i]);
		i > 8 ? i = 0 : i++;
		delay(500);
		digitalWrite(warn_LED, LOW);
		delay(1000);
	}
}
